// Logisim project proccessor.circ as structural Verilog: 22 circuits, main circuit main
module main (
);

  FULL_ADDER_4BIT full_adder_4bit_1 ();  // open: CARRY_IN, A, A_1, A_2, A_3, B, B_1, B_2, B_3, Y, Y_1, Y_2, Y_3, CARRY_OUT
endmodule

module HALF_ADDER (
  input  A,
  input  B,
  output SUM,
  output CARRY
);

  xor xor_1 (SUM, A, B);
  and and_1 (CARRY, A, B);
endmodule

module INC_4BIT (
  input  A,
  input  A_1,
  input  A_2,
  input  A_3,
  input  INC,
  output Y,
  output Y_1,
  output Y_2,
  output Y_3,
  output CARRY
);

  wire half_adder_1_carry, half_adder_2_carry, half_adder_3_carry;

  HALF_ADDER half_adder_1 (.A(INC), .B(A), .SUM(Y), .CARRY(half_adder_1_carry));
  HALF_ADDER half_adder_2 (.A(half_adder_1_carry), .B(A_1), .SUM(Y_1), .CARRY(half_adder_2_carry));
  HALF_ADDER half_adder_3 (.A(half_adder_2_carry), .B(A_2), .SUM(Y_2), .CARRY(half_adder_3_carry));
  HALF_ADDER half_adder_4 (.A(half_adder_3_carry), .B(A_3), .SUM(Y_3), .CARRY(CARRY));
endmodule

module tows_comp (
  input  A,
  input  A_1,
  input  A_2,
  input  A_3,
  output Y,
  output Y_1,
  output Y_2,
  output Y_3,
  output CARRY
);

  wire not_1_out, not_2_out, not_3_out, not_4_out;

  not not_1 (not_1_out, A);
  not not_2 (not_2_out, A_1);
  not not_3 (not_3_out, A_2);
  not not_4 (not_4_out, A_3);
  INC_4BIT inc_4bit_1 (
    .A(not_1_out), .A_1(not_2_out), .A_2(not_3_out), .A_3(not_4_out), .INC(1'b1), .Y(Y), .Y_1(Y_1),
    .Y_2(Y_2), .Y_3(Y_3), .CARRY(CARRY));
endmodule

module FULL_ADDER_1BIT (
  input  CARRY_IN,
  input  B,
  input  A,
  output SUM,
  output CARRY_OUT
);

  wire or_1_out, or_2_out, or_3_out;

  or or_1 (or_1_out, A, B);
  or or_2 (or_2_out, A, CARRY_IN);
  or or_3 (or_3_out, B, CARRY_IN);
  xor xor_1 (SUM, CARRY_IN, B, A);
  and and_1 (CARRY_OUT, or_1_out, or_2_out, or_3_out);
endmodule

module FULL_ADDER_4BIT (
  input  CARRY_IN,
  input  A,
  input  A_1,
  input  A_2,
  input  A_3,
  input  B,
  input  B_1,
  input  B_2,
  input  B_3,
  output Y,
  output Y_1,
  output Y_2,
  output Y_3,
  output CARRY_OUT
);

  wire full_adder_1bit_1_carry_out, full_adder_1bit_2_carry_out, full_adder_1bit_3_carry_out;

  FULL_ADDER_1BIT full_adder_1bit_1 (
    .CARRY_IN(CARRY_IN), .B(B), .A(A), .SUM(Y), .CARRY_OUT(full_adder_1bit_1_carry_out));
  FULL_ADDER_1BIT full_adder_1bit_2 (
    .CARRY_IN(full_adder_1bit_1_carry_out), .B(B_1), .A(A_1), .SUM(Y_1),
    .CARRY_OUT(full_adder_1bit_2_carry_out));
  FULL_ADDER_1BIT full_adder_1bit_3 (
    .CARRY_IN(full_adder_1bit_2_carry_out), .B(B_2), .A(A_2), .SUM(Y_2),
    .CARRY_OUT(full_adder_1bit_3_carry_out));
  FULL_ADDER_1BIT full_adder_1bit_4 (
    .CARRY_IN(full_adder_1bit_3_carry_out), .B(B_3), .A(A_3), .SUM(Y_3), .CARRY_OUT(CARRY_OUT));
endmodule

module MUX_1BIT (
  input  A,
  input  B,
  input  A_notB,
  output Y
);

  wire and_1_out, and_2_out, not_1_out;

  not not_1 (not_1_out, A_notB);
  and and_1 (and_1_out, A, A_notB);
  and and_2 (and_2_out, not_1_out, B);
  or or_1 (Y, and_1_out, and_2_out);
endmodule

module MUX_4BIT (
  input  A,
  input  A_1,
  input  A_2,
  input  A_3,
  input  B,
  input  B_1,
  input  B_2,
  input  B_3,
  input  A_notB,
  output Y,
  output Y_1,
  output Y_2,
  output Y_3
);

  MUX_1BIT mux_1bit_1 (.A(A), .B(B), .A_notB(A_notB), .Y(Y));
  MUX_1BIT mux_1bit_2 (.A(A_1), .B(B_1), .A_notB(A_notB), .Y(Y_1));
  MUX_1BIT mux_1bit_3 (.A(A_2), .B(B_2), .A_notB(A_notB), .Y(Y_2));
  MUX_1BIT mux_1bit_4 (.A(A_3), .B(B_3), .A_notB(A_notB), .Y(Y_3));
endmodule

module DECODER1_2 (
  input  A0,
  input  ENABLE,
  output Y0,
  output Y1
);

  wire not_1_out;

  not not_1 (not_1_out, A0);
  and and_1 (Y0, not_1_out, ENABLE);
  and and_2 (Y1, A0, ENABLE);
endmodule

module DECODER2_4 (
  input  A0,
  input  A1,
  input  ENABLE,
  output Y,
  output Y_1,
  output Y_2,
  output Y_3
);

  wire decoder1_2_1_y0, decoder1_2_1_y1;

  DECODER1_2 decoder1_2_1 (.A0(A1), .ENABLE(ENABLE), .Y0(decoder1_2_1_y0), .Y1(decoder1_2_1_y1));
  DECODER1_2 decoder1_2_2 (.A0(A0), .ENABLE(decoder1_2_1_y0), .Y0(Y), .Y1(Y_1));
  DECODER1_2 decoder1_2_3 (.A0(A0), .ENABLE(decoder1_2_1_y1), .Y0(Y_2), .Y1(Y_3));
endmodule

module DECODER4_16 (
  input  A,
  input  A_1,
  input  A_2,
  input  A_3,
  input  ENABLE,
  output Y,
  output Y_1,
  output Y_2,
  output Y_3,
  output Y_4,
  output Y_5,
  output Y_6,
  output Y_7,
  output Y_8,
  output Y_9,
  output Y_10,
  output Y_11,
  output Y_12,
  output Y_13,
  output Y_14,
  output Y_15
);

  wire decoder2_4_1_y, decoder2_4_1_y_1, decoder2_4_1_y_2, decoder2_4_1_y_3;

  DECODER2_4 decoder2_4_1 (
    .A0(A_2), .A1(A_3), .ENABLE(ENABLE), .Y(decoder2_4_1_y), .Y_1(decoder2_4_1_y_1), .Y_2(decoder2_4_1_y_2),
    .Y_3(decoder2_4_1_y_3));
  DECODER2_4 decoder2_4_2 (.A0(A), .A1(A_1), .ENABLE(decoder2_4_1_y), .Y(Y), .Y_1(Y_1), .Y_2(Y_2), .Y_3(Y_3));
  DECODER2_4 decoder2_4_3 (.A0(A), .A1(A_1), .ENABLE(decoder2_4_1_y_1), .Y(Y_4), .Y_1(Y_5), .Y_2(Y_6), .Y_3(Y_7));
  DECODER2_4 decoder2_4_4 (.A0(A), .A1(A_1), .ENABLE(decoder2_4_1_y_2), .Y(Y_8), .Y_1(Y_9), .Y_2(Y_10), .Y_3(Y_11));
  DECODER2_4 decoder2_4_5 (.A0(A), .A1(A_1), .ENABLE(decoder2_4_1_y_3), .Y(Y_12), .Y_1(Y_13), .Y_2(Y_14), .Y_3(Y_15));
endmodule

module NOT_NEG (
  input  A,
  input  A_1,
  input  A_2,
  input  A_3,
  input  notPASS,
  input  NOT_notNEG,
  output Y,
  output Y_1,
  output Y_2,
  output Y_3,
  output CARRY_OUT
);

  wire and_1_out, not_1_out, xor_1_out, xor_2_out, xor_3_out, xor_4_out;

  not not_1 (not_1_out, NOT_notNEG);
  xor xor_1 (xor_1_out, A, notPASS);
  xor xor_2 (xor_2_out, A_1, notPASS);
  xor xor_3 (xor_3_out, A_2, notPASS);
  xor xor_4 (xor_4_out, A_3, notPASS);
  and and_1 (and_1_out, notPASS, not_1_out);
  INC_4BIT inc_4bit_1 (
    .A(xor_1_out), .A_1(xor_2_out), .A_2(xor_3_out), .A_3(xor_4_out), .INC(and_1_out), .Y(Y), .Y_1(Y_1),
    .Y_2(Y_2), .Y_3(Y_3), .CARRY(CARRY_OUT));
endmodule

module XOR_ADD (
  input  A,
  input  A_1,
  input  A_2,
  input  A_3,
  input  B,
  input  B_1,
  input  B_2,
  input  B_3,
  input  XOR_notADD,
  input  not_PASS,
  input  CARRY_IN,
  output Y,
  output Y_1,
  output Y_2,
  output Y_3,
  output COUT
);

  wire mux_4bit_1_y, mux_4bit_1_y_1, mux_4bit_1_y_2, mux_4bit_1_y_3;
  wire [3:0] full_adder_4bit_1_y, xor_1_out;

  xor xor_1 (xor_1_out[0], A, B);
  xor xor_2 (xor_1_out[1], A_1, B_1);
  xor xor_3 (xor_1_out[2], A_2, B_2);
  xor xor_4 (xor_1_out[3], A_3, B_3);
  FULL_ADDER_4BIT full_adder_4bit_1 (
    .CARRY_IN(CARRY_IN), .A(A), .A_1(A_1), .A_2(A_2), .A_3(A_3), .B(B), .B_1(B_1), .B_2(B_2), .B_3(B_3),
    .Y(full_adder_4bit_1_y[0]), .Y_1(full_adder_4bit_1_y[1]), .Y_2(full_adder_4bit_1_y[2]),
    .Y_3(full_adder_4bit_1_y[3]), .CARRY_OUT(COUT));
  MUX_4BIT mux_4bit_1 (
    .A(xor_1_out[0]), .A_1(xor_1_out[1]), .A_2(xor_1_out[2]), .A_3(xor_1_out[3]), .B(full_adder_4bit_1_y[0]),
    .B_1(full_adder_4bit_1_y[1]), .B_2(full_adder_4bit_1_y[2]), .B_3(full_adder_4bit_1_y[3]),
    .A_notB(XOR_notADD), .Y(mux_4bit_1_y), .Y_1(mux_4bit_1_y_1), .Y_2(mux_4bit_1_y_2), .Y_3(mux_4bit_1_y_3));
  MUX_4BIT mux_4bit_2 (
    .A(mux_4bit_1_y), .A_1(mux_4bit_1_y_1), .A_2(mux_4bit_1_y_2), .A_3(mux_4bit_1_y_3), .B(A), .B_1(A_1),
    .B_2(A_2), .B_3(A_3), .A_notB(not_PASS), .Y(Y), .Y_1(Y_1), .Y_2(Y_2), .Y_3(Y_3));

  // Other names for the same wires on the sheet: A_t[3:0] = {A_3, A_2, A_1, A}; B_t[3:0] = {B_3, B_2, B_1, B};
  //   C_IN = CARRY_IN
endmodule

module ALU (
  input  A,
  input  A_1,
  input  A_2,
  input  A_3,
  input  B,
  input  B_1,
  input  B_2,
  input  B_3,
  input  CARRY_IN,
  input  LOGIC_notARITH,
  input  notINVERT,
  input  notAONLY,
  output Y,
  output Y_1,
  output Y_2,
  output Y_3,
  output COUT
);

  wire not_1_out, not_neg_1_y, not_neg_1_y_1, not_neg_1_y_2, not_neg_1_y_3;

  not not_1 (not_1_out, notINVERT);
  NOT_NEG not_neg_1 (
    .A(A), .A_1(A_1), .A_2(A_2), .A_3(A_3), .notPASS(not_1_out), .NOT_notNEG(LOGIC_notARITH),
    .Y(not_neg_1_y), .Y_1(not_neg_1_y_1), .Y_2(not_neg_1_y_2), .Y_3(not_neg_1_y_3));  // open: CARRY_OUT
  XOR_ADD xor_add_1 (
    .A(not_neg_1_y), .A_1(not_neg_1_y_1), .A_2(not_neg_1_y_2), .A_3(not_neg_1_y_3), .B(B), .B_1(B_1),
    .B_2(B_2), .B_3(B_3), .XOR_notADD(LOGIC_notARITH), .not_PASS(notAONLY), .CARRY_IN(CARRY_IN), .Y(Y),
    .Y_1(Y_1), .Y_2(Y_2), .Y_3(Y_3), .COUT(COUT));

  // Other names for the same wires on the sheet: CIN = CARRY_IN
endmodule

module REGISTER_1BIT (
  input  DATA,
  input  ENABLE,
  input  CLOCK,
  input  CLEAR,
  output OUT_PUT
);

  wire and_1_out, and_2_out, not_1_out;

  not not_1 (not_1_out, DATA);
  and and_1 (and_1_out, DATA, ENABLE);
  and and_2 (and_2_out, not_1_out, ENABLE);
  J_K_Flip_Flop #(.trigger("falling")) j_k_ff_1 (
    .J(and_1_out), .K(and_2_out), .clk(CLOCK), .Q(OUT_PUT), .preset(1'b0), .reset(CLEAR));  // open: Qn
endmodule

module REGISTER_4BIT (
  input  A,
  input  A_1,
  input  A_2,
  input  A_3,
  input  ENABLE,
  input  CLOCK,
  input  CLEAR,
  output Y,
  output Y_1,
  output Y_2,
  output Y_3
);

  REGISTER_1BIT register_1bit_1 (.DATA(A), .ENABLE(ENABLE), .CLOCK(CLOCK), .CLEAR(CLEAR), .OUT_PUT(Y));
  REGISTER_1BIT register_1bit_2 (.DATA(A_1), .ENABLE(ENABLE), .CLOCK(CLOCK), .CLEAR(CLEAR), .OUT_PUT(Y_1));
  REGISTER_1BIT register_1bit_3 (.DATA(A_2), .ENABLE(ENABLE), .CLOCK(CLOCK), .CLEAR(CLEAR), .OUT_PUT(Y_2));
  REGISTER_1BIT register_1bit_4 (.DATA(A_3), .ENABLE(ENABLE), .CLOCK(CLOCK), .CLEAR(CLEAR), .OUT_PUT(Y_3));
endmodule

module BUFFER_4BIT (
  input  A,
  input  A_1,
  input  A_2,
  input  A_3,
  input  ENABLE1,
  input  ENABLE2,
  output Y,
  output Y_1,
  output Y_2,
  output Y_3
);

  BUFFER_1BIT buffer_1bit_1 (.A(A), .ENABLE1(ENABLE1), .ENABLE2(ENABLE2), .Y(Y));
  BUFFER_1BIT buffer_1bit_2 (.A(A_1), .ENABLE1(ENABLE1), .ENABLE2(ENABLE2), .Y(Y_1));
  BUFFER_1BIT buffer_1bit_3 (.A(A_2), .ENABLE1(ENABLE1), .ENABLE2(ENABLE2), .Y(Y_2));
  BUFFER_1BIT buffer_1bit_4 (.A(A_3), .ENABLE1(ENABLE1), .ENABLE2(ENABLE2), .Y(Y_3));
endmodule

module BUFFER_1BIT (
  input  A,
  input  ENABLE1,
  input  ENABLE2,
  output Y
);

  wire and_1_out;

  and and_1 (and_1_out, ENABLE1, ENABLE2);
  assign Y = and_1_out ? A : 1'bz;  // Controlled_Buffer controlled_buffer_1
endmodule

module ROM_4CELLS_4BIT (
  input  [3:0] MEM_SELECT,
  input  READ,
  input  [3:0] D,
  input  [3:0] D_1,
  input  [3:0] D_2,
  input  [3:0] D_3,
  output [3:0] DATA
);

  BUFFER_4BIT buffer_4bit_1 (
    .A(D[0]), .A_1(D[1]), .A_2(D[2]), .A_3(D[3]), .ENABLE1(MEM_SELECT[0]), .ENABLE2(READ), .Y(DATA[0]),
    .Y_1(DATA[1]), .Y_2(DATA[2]), .Y_3(DATA[3]));
  BUFFER_4BIT buffer_4bit_2 (
    .A(D_1[0]), .A_1(D_1[1]), .A_2(D_1[2]), .A_3(D_1[3]), .ENABLE1(MEM_SELECT[1]), .ENABLE2(READ),
    .Y(DATA[0]), .Y_1(DATA[1]), .Y_2(DATA[2]), .Y_3(DATA[3]));
  BUFFER_4BIT buffer_4bit_3 (
    .A(D_2[0]), .A_1(D_2[1]), .A_2(D_2[2]), .A_3(D_2[3]), .ENABLE1(MEM_SELECT[2]), .ENABLE2(READ),
    .Y(DATA[0]), .Y_1(DATA[1]), .Y_2(DATA[2]), .Y_3(DATA[3]));
  BUFFER_4BIT buffer_4bit_4 (
    .A(D_3[0]), .A_1(D_3[1]), .A_2(D_3[2]), .A_3(D_3[3]), .ENABLE1(MEM_SELECT[3]), .ENABLE2(READ),
    .Y(DATA[0]), .Y_1(DATA[1]), .Y_2(DATA[2]), .Y_3(DATA[3]));
endmodule

module MEM_ADD_GENERATION (
  input  [3:0] DATA_BUS,
  input  USE_PC,
  input  LOAD_MAR,
  input  CLOCK,
  input  RESET,
  output [3:0] ADDRESS_BUS
);

  wire inc_4bit_1_y, inc_4bit_1_y_1, inc_4bit_1_y_2, inc_4bit_1_y_3;
  wire [3:0] MAR_y, PC_y;

  INC_4BIT inc_4bit_1 (
    .A(PC_y[0]), .A_1(PC_y[1]), .A_2(PC_y[2]), .A_3(PC_y[3]), .INC(1'b1), .Y(inc_4bit_1_y),
    .Y_1(inc_4bit_1_y_1), .Y_2(inc_4bit_1_y_2), .Y_3(inc_4bit_1_y_3));  // open: CARRY
  REGISTER_4BIT PC (
    .A(inc_4bit_1_y), .A_1(inc_4bit_1_y_1), .A_2(inc_4bit_1_y_2), .A_3(inc_4bit_1_y_3), .ENABLE(USE_PC),
    .CLOCK(CLOCK), .CLEAR(RESET), .Y(PC_y[0]), .Y_1(PC_y[1]), .Y_2(PC_y[2]), .Y_3(PC_y[3]));
  Hex_Digit_Display hex_digit_display_1 (.value(PC_y));  // open: dp
  REGISTER_4BIT MAR (
    .A(DATA_BUS[0]), .A_1(DATA_BUS[1]), .A_2(DATA_BUS[2]), .A_3(DATA_BUS[3]), .ENABLE(LOAD_MAR),
    .CLOCK(CLOCK), .CLEAR(RESET), .Y(MAR_y[0]), .Y_1(MAR_y[1]), .Y_2(MAR_y[2]), .Y_3(MAR_y[3]));
  MUX_4BIT mux_4bit_1 (
    .A(PC_y[0]), .A_1(PC_y[1]), .A_2(PC_y[2]), .A_3(PC_y[3]), .B(MAR_y[0]), .B_1(MAR_y[1]), .B_2(MAR_y[2]),
    .B_3(MAR_y[3]), .A_notB(USE_PC), .Y(ADDRESS_BUS[0]), .Y_1(ADDRESS_BUS[1]), .Y_2(ADDRESS_BUS[2]),
    .Y_3(ADDRESS_BUS[3]));
endmodule

module CONTROL_CIRCUIT (
  input  [3:0] DATA_BUS,
  input  CLOCK,
  input  RESET,
  output ID3,
  output ID4,
  output ID5,
  output ID6,
  output ID7,
  output ID8,
  output ID9,
  output ID10,
  output ID11,
  output ID12,
  output ID13,
  output ID14,
  output ID15
);

  wire ID2;
  wire [1:0] rom_1_data;
  wire [3:0] register_4bit_1_y_2, register_4bit_2_y;

  REGISTER_4BIT register_4bit_1 (
    .A(rom_1_data[0]), .A_1(rom_1_data[1]), .A_2(1'b0), .A_3(1'b0), .ENABLE(1'b1), .CLOCK(CLOCK),
    .CLEAR(RESET), .Y(register_4bit_1_y_2[0]), .Y_1(register_4bit_1_y_2[1]), .Y_2(register_4bit_1_y_2[2]),
    .Y_3(register_4bit_1_y_2[3]));
  Hex_Digit_Display hex_digit_display_1 (.value(register_4bit_2_y));  // open: dp
  REGISTER_4BIT register_4bit_2 (
    .A(DATA_BUS[0]), .A_1(DATA_BUS[1]), .A_2(DATA_BUS[2]), .A_3(DATA_BUS[3]), .ENABLE(ID2), .CLOCK(CLOCK),
    .CLEAR(RESET), .Y(register_4bit_2_y[0]), .Y_1(register_4bit_2_y[1]), .Y_2(register_4bit_2_y[2]),
    .Y_3(register_4bit_2_y[3]));
  Hex_Digit_Display hex_digit_display_2 (.value(register_4bit_1_y_2));  // open: dp
  ROM #(.addrWidth(6), .dataWidth(16)) rom_1 (
    .addr({register_4bit_2_y, register_4bit_1_y_2[1:0]}),
    .data({ID15, ID14, ID13, ID12, ID11, ID10, ID9, ID8, ID7, ID6, ID5, ID4, ID3, ID2, rom_1_data}));

  // Notes on the sheet:
  //   contents of rom_1 (hex, n*v repeats v):
  //   115 550 0 0 115 750 0 0 115 1
  //   LOAD IR
  //   NEXT STATE BIT 0
  //   NEXT STATE BIT1
endmodule

module BRAINLESS_CPU (
  input  [3:0] in_1,
  input  [3:0] in_2,
  input  [3:0] in_3,
  input  [3:0] in_4,
  input  [3:0] in_5,
  input  CLOCK,
  input  [3:0] in_7,
  input  [3:0] in_8,
  input  RESET,
  input  [3:0] in_10
);

  wire ACC_TO_DB, AD14, AD15, and_1_out, and_2_out, LOAD_ACC, LOAD_MAR, READ, register_4bit_3_y,
       register_4bit_3_y_1, register_4bit_3_y_2, register_4bit_3_y_3, USE_PC, WRITE;
  wire [2:0] A_LU;
  wire [3:0] alu_1_y, buffer_4bit_1_y, mem_add_generation_1_address_bus, register_4bit_1_y, register_4bit_2_y;
  wire [7:0] decoder4_16_1_y;

  ALU alu_1 (
    .A(buffer_4bit_1_y[0]), .A_1(buffer_4bit_1_y[1]), .A_2(buffer_4bit_1_y[2]), .A_3(buffer_4bit_1_y[3]),
    .B(register_4bit_1_y[0]), .B_1(register_4bit_1_y[1]), .B_2(register_4bit_1_y[2]),
    .B_3(register_4bit_1_y[3]), .CARRY_IN(1'b0), .LOGIC_notARITH(A_LU[2]), .notINVERT(A_LU[1]),
    .notAONLY(A_LU[0]), .Y(alu_1_y[0]), .Y_1(alu_1_y[1]), .Y_2(alu_1_y[2]), .Y_3(alu_1_y[3]));  // open: COUT
  CONTROL_CIRCUIT control_circuit_1 (
    .DATA_BUS(buffer_4bit_1_y), .CLOCK(CLOCK), .RESET(RESET), .ID3(WRITE), .ID4(READ), .ID5(ACC_TO_DB),
    .ID6(LOAD_ACC), .ID7(LOAD_MAR), .ID8(USE_PC), .ID9(A_LU[0]), .ID10(A_LU[1]), .ID11(A_LU[2]));  // open: ID12, ID13, ID14, ID15
  Hex_Digit_Display hex_digit_display_1 (.value(alu_1_y));  // open: dp
  MEM_ADD_GENERATION mem_add_generation_1 (
    .DATA_BUS(buffer_4bit_1_y), .USE_PC(USE_PC), .LOAD_MAR(LOAD_MAR), .CLOCK(CLOCK), .RESET(RESET),
    .ADDRESS_BUS(mem_add_generation_1_address_bus));
  REGISTER_4BIT register_4bit_1 (
    .A(alu_1_y[0]), .A_1(alu_1_y[1]), .A_2(alu_1_y[2]), .A_3(alu_1_y[3]), .ENABLE(LOAD_ACC), .CLOCK(CLOCK),
    .CLEAR(RESET), .Y(register_4bit_1_y[0]), .Y_1(register_4bit_1_y[1]), .Y_2(register_4bit_1_y[2]),
    .Y_3(register_4bit_1_y[3]));
  Hex_Digit_Display hex_digit_display_2 (.value(register_4bit_1_y));  // open: dp
  Hex_Digit_Display hex_digit_display_3 (.value(mem_add_generation_1_address_bus));  // open: dp
  Hex_Digit_Display hex_digit_display_4 (.value(buffer_4bit_1_y));  // open: dp
  BUFFER_4BIT buffer_4bit_1 (
    .A(register_4bit_1_y[0]), .A_1(register_4bit_1_y[1]), .A_2(register_4bit_1_y[2]),
    .A_3(register_4bit_1_y[3]), .ENABLE1(ACC_TO_DB), .ENABLE2(ACC_TO_DB), .Y(buffer_4bit_1_y[0]),
    .Y_1(buffer_4bit_1_y[1]), .Y_2(buffer_4bit_1_y[2]), .Y_3(buffer_4bit_1_y[3]));
  and and_1 (and_1_out, AD14, WRITE);
  and and_2 (and_2_out, WRITE, AD15);
  DECODER4_16 decoder4_16_1 (
    .A(mem_add_generation_1_address_bus[0]), .A_1(mem_add_generation_1_address_bus[1]),
    .A_2(mem_add_generation_1_address_bus[2]), .A_3(mem_add_generation_1_address_bus[3]), .ENABLE(1'b1),
    .Y(decoder4_16_1_y[0]), .Y_1(decoder4_16_1_y[1]), .Y_2(decoder4_16_1_y[2]), .Y_3(decoder4_16_1_y[3]),
    .Y_4(decoder4_16_1_y[4]), .Y_5(decoder4_16_1_y[5]), .Y_6(decoder4_16_1_y[6]), .Y_7(decoder4_16_1_y[7]),
    .Y_14(AD14), .Y_15(AD15));  // open: Y_8, Y_9, Y_10, Y_11, Y_12, Y_13
  Hex_Digit_Display hex_digit_display_5 (.value(register_4bit_2_y));  // open: dp
  REGISTER_4BIT register_4bit_2 (
    .A(buffer_4bit_1_y[0]), .A_1(buffer_4bit_1_y[1]), .A_2(buffer_4bit_1_y[2]), .A_3(buffer_4bit_1_y[3]),
    .ENABLE(and_1_out), .CLOCK(CLOCK), .CLEAR(RESET), .Y(register_4bit_2_y[0]), .Y_1(register_4bit_2_y[1]),
    .Y_2(register_4bit_2_y[2]), .Y_3(register_4bit_2_y[3]));
  REGISTER_4BIT register_4bit_3 (
    .A(buffer_4bit_1_y[0]), .A_1(buffer_4bit_1_y[1]), .A_2(buffer_4bit_1_y[2]), .A_3(buffer_4bit_1_y[3]),
    .ENABLE(and_2_out), .CLOCK(CLOCK), .CLEAR(RESET), .Y(register_4bit_3_y), .Y_1(register_4bit_3_y_1),
    .Y_2(register_4bit_3_y_2), .Y_3(register_4bit_3_y_3));
  BUFFER_4BIT buffer_4bit_2 (
    .A(register_4bit_3_y), .A_1(register_4bit_3_y_1), .A_2(register_4bit_3_y_2), .A_3(register_4bit_3_y_3),
    .ENABLE1(READ), .ENABLE2(AD15), .Y(buffer_4bit_1_y[0]), .Y_1(buffer_4bit_1_y[1]),
    .Y_2(buffer_4bit_1_y[2]), .Y_3(buffer_4bit_1_y[3]));
  ROM_4CELLS_4BIT rom_4cells_4bit_1 (
    .MEM_SELECT(decoder4_16_1_y[3:0]), .READ(READ), .D(in_1), .D_1(in_2), .D_2(in_3), .D_3(in_4),
    .DATA(buffer_4bit_1_y));
  ROM_4CELLS_4BIT rom_4cells_4bit_2 (
    .MEM_SELECT(decoder4_16_1_y[7:4]), .READ(READ), .D(in_5), .D_1(in_7), .D_2(in_8), .D_3(in_10),
    .DATA(buffer_4bit_1_y));

  // Other names for the same wires on the sheet: CLCK = CLOCK

  // Notes on the sheet:
  //   DATA BUS
  //   MEMORY SELECT LINE
endmodule
